// Logisim project exp5.circ as structural Verilog: 1 circuit, main circuit main
module main (
);

  wire [2:0] adder_1_out, multiplexer_1_out, not_1_out;
  wire [3:3] adder_1_out_2;

  assign not_1_out = ~adder_1_out;  // NOT_Gate not_1, 3 bits wide
  Multiplexer #(.width(3), .enable("false")) multiplexer_1 (
    .in0(3'b101), .in1(not_1_out), .out(multiplexer_1_out), .sel(1'b1));
  // Probe on multiplexer_1_out
  Adder #(.width(4)) adder_1 (.a(4'b1101), .b(4'b1111), .out({adder_1_out_2[3], adder_1_out}));  // open: cin, cout
endmodule
