// Logisim project exp7.circ as structural Verilog: 1 circuit, main circuit main
module main (
);

  wire A, A_2_qn, A_q, AB_2_out, AB_out, ABC_2_out, ABC_out, B, B_q, C, C_q, CLK, clock_1_out,
       comparator_1_eq, comparator_2_eq, D, D_q, j_k_ff_1_qn, j_k_ff_2_qn, multiplexer_1_out,
       multiplexer_2_out, multiplexer_3_out, MUX, nAB_tilde_out, nABC_tilde_out;

  Clock clock_1 (.out(clock_1_out));
  J_K_Flip_Flop u_A (.J(1'b1), .clk(clock_1_out), .K(1'b1), .Q(A_q));  // open: Qn, preset, en, reset
  J_K_Flip_Flop A_2 (.J(1'b1), .clk(CLK), .K(1'b1), .Q(A), .Qn(A_2_qn));  // open: preset, en, reset
  J_K_Flip_Flop u_B (.J(A_q), .clk(clock_1_out), .K(A_q), .Q(B_q));  // open: Qn, preset, en, reset
  // Probe on B_q
  // Probe on C_q
  // Probe on A_q
  Multiplexer #(.enable("false")) multiplexer_1 (.in0(A), .in1(A_2_qn), .out(multiplexer_1_out), .sel(MUX));
  and AB (AB_out, A_q, B_q);
  // Probe on D_q
  J_K_Flip_Flop u_C (.J(AB_out), .clk(clock_1_out), .K(AB_out), .Q(C_q));  // open: Qn, preset, en, reset
  J_K_Flip_Flop j_k_ff_1 (
    .J(multiplexer_1_out), .clk(CLK), .K(multiplexer_1_out), .Q(B), .Qn(j_k_ff_1_qn));  // open: preset, en, reset
  and ABC (ABC_out, A_q, B_q, C_q);
  J_K_Flip_Flop u_D (.J(ABC_out), .clk(clock_1_out), .K(ABC_out), .Q(D_q));  // open: Qn, preset, en, reset
  and nAB_tilde (nAB_tilde_out, A_2_qn, j_k_ff_1_qn);
  and AB_2 (AB_2_out, A, B);
  // Probe on {D, C, B, A}
  Clock clock_2 (.out(CLK));
  Multiplexer #(.enable("false")) multiplexer_2 (
    .in0(AB_2_out), .in1(nAB_tilde_out), .out(multiplexer_2_out), .sel(MUX));
  and nABC_tilde (nABC_tilde_out, nAB_tilde_out, j_k_ff_2_qn);
  J_K_Flip_Flop j_k_ff_2 (
    .J(multiplexer_2_out), .clk(CLK), .K(multiplexer_2_out), .Q(C), .Qn(j_k_ff_2_qn));  // open: preset, en, reset
  Comparator #(.width(4)) comparator_1 (.a({D, C, B, A}), .b(4'b0000), .eq(comparator_1_eq));  // open: gt, lt
  Comparator #(.width(4)) comparator_2 (.a({D, C, B, A}), .b(4'b1000), .eq(comparator_2_eq));  // open: gt, lt
  and ABC_2 (ABC_2_out, A, B, C);
  Multiplexer #(.enable("false")) multiplexer_3 (
    .in0(ABC_2_out), .in1(nABC_tilde_out), .out(multiplexer_3_out), .sel(MUX));
  D_Flip_Flop d_ff_1 (.clk(CLK), .D(MUX), .Q(MUX), .preset(comparator_2_eq), .reset(comparator_1_eq));  // open: Qn, en
  J_K_Flip_Flop j_k_ff_3 (
    .J(multiplexer_3_out), .clk(CLK), .K(multiplexer_3_out), .Q(D));  // open: Qn, preset, en, reset
endmodule
